# Fritzing sketch Esquema Electrico HubUsbBotonesArduino (saved by Fritzing 0.9.3b)
circuit board: 8.46667cm x 5.64444cm
breadboards: 1

parts:
  Componente1 = Arduino Nano (Rev3.0)
  S1 = Pushbutton [package="[THT]"]
  LED1 = LED - 5mm [color="Blue (525nm)" package="5 mm [THT]"]
  LED2 = LED - 5mm [color="Red (633nm)" package="5 mm [THT]"]
  4_Relay_Module1 = OPENMolo 4 Relay breakout board
  R3 = Resistor [tolerance=±5% resistance=220 package=THT]
  R1 = Resistor [tolerance=±5% resistance=220 package="2010 [SMD]"]
  R2 = Resistor [tolerance=±5% resistance=220 package="0805 [SMD]"]
  Power_plug1 = Power plug
  U2 = USB Connectors [package=usb-a-s-silk-female]
  U3 = USB Connectors [package=usb-a-h]
  U4 = USB Connectors [package=usb-a-h]

nets:
  N1: Componente1.D2, S1.Pin_4
  GND: Componente1.GND, LED1.cathode, LED2.cathode, 4_Relay_Module1.GND, 4_Relay_Module1.E4, 4_Relay_Module1.E3, 4_Relay_Module1.E2, 4_Relay_Module1.E1, R3.Pin_1, Power_plug1.GND
  N2: Componente1.A2, 4_Relay_Module1.VCC, R2.Pin_0
  N3: Componente1.A1, R1.Pin_0
  N4: Componente1.3V3, S1.Pin_1, S1.Pin_2, R3.Pin_0
  N5: LED1.anode, R1.Pin_1
  N6: LED2.anode, R2.Pin_1
  N7: 4_Relay_Module1.P_VCC, Power_plug1.VCC
  N8: 4_Relay_Module1.NC_Rel_1, U3.GND
  N9: 4_Relay_Module1.PW_Rel_1, U2.GND
  N10: 4_Relay_Module1.NO_Rel_1, U4.GND
  N11: 4_Relay_Module1.NC_Rel_2, U3.D+
  N12: 4_Relay_Module1.PW_Rel_R2, U2.D+
  N13: 4_Relay_Module1.NO_Rel_2, U4.D+
  N14: 4_Relay_Module1.NC_Rel_3, U3.D-
  N15: 4_Relay_Module1.PW_Rel_3, U2.D-
  N16: 4_Relay_Module1.NO_Rel_3, U4.D-
  N17: 4_Relay_Module1.NC_Rel_4, U3.VBUS
  N18: 4_Relay_Module1.PW_Rel_4, U2.VBUS
  N19: 4_Relay_Module1.NO_Rel_4, U4.VBUS

custom parts:
  OPENMolo 4 Relay breakout board: Módulo de 8 relés de 10A optoaislados pensado para desarrollos rápidos basadon en microcontroladores o microcomputadoras. Estos módulos son diseñados con especial cuidado tanto en sus capacidades aisladoras para preservar equipos de mayor valor asi como en las fijaciones para evitar problemas a la hora de armar un prototipo o de fijarlo en un tablero definitivo. Una importante característica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
